// Logisim project 8bitcomputer.circ as structural Verilog: 4 circuits, main circuit main
module main (
  input  ENABLE,
  input  SUB,
  input  ENABLE_2,
  input  ENABLE_3,
  input  [7:0] in_5,
  input  ENABLE_4,
  output [7:0] OUTPUT
);

  wire alu_main_1_p3, alu_main_1_p4, n1bitregister_1_p1;

  assign OUTPUT = ENABLE_4 ? in_5 : 8'bz;  // Controlled_Buffer controlled_buffer_1
  // alu_main alu_main_1: pin names not known; wires that end beside it: OUTPUT, ENABLE_3, alu_main_1_p3, alu_main_1_p4, SUB, ENABLE_2
  // _1bitregister 1bitregister_1: pin names not known; wires that end beside it: n1bitregister_1_p1, alu_main_1_p3
  // _1bitregister 1bitregister_2: pin names not known; wires that end beside it: n1bitregister_1_p1, alu_main_1_p4
  Clock clock_1 (.out(n1bitregister_1_p1));

  // Notes on the sheet:
  //   INPUT
  //   BUS
  //   REGISTER A
  //   REGISTER B
endmodule

module full__adder (
  input  A,
  input  B,
  input  Cin,
  output S,
  output Co
);

  wire and_1_out, and_2_out, and_3_out, and_4_out, and_5_out, and_6_out, not_1_out, not_2_out, not_3_out,
       not_4_out, or_1_out;

  not not_1 (not_1_out, B);
  not not_2 (not_2_out, A);
  and and_1 (and_1_out, not_1_out, A);
  and and_2 (and_2_out, B, not_2_out);
  or or_1 (or_1_out, and_1_out, and_2_out);
  and and_3 (and_3_out, A, B);
  not not_3 (not_3_out, Cin);
  not not_4 (not_4_out, or_1_out);
  and and_4 (and_4_out, Cin, or_1_out);
  and and_5 (and_5_out, not_3_out, or_1_out);
  and and_6 (and_6_out, not_4_out, Cin);
  or or_2 (Co, and_4_out, and_3_out);
  or or_3 (S, and_5_out, and_6_out);

  // Notes on the sheet:
  //   A
  //   B
  //   Cin
  //   S
  //   Co
endmodule

module _4_b (
  input  in_1,
  input  in_2,
  input  in_3,
  input  in_4,
  input  in_5,
  input  B0,
  input  in_7,
  input  in_8,
  input  in_9,
  output out_10,
  output out_11,
  output out_12,
  output out_13,
  output out_14
);

  wire and_1_out, and_4_out, and_5_out, and_6_out, and_9_out, and_10_out, and_11_out, and_12_out, and_13_out,
       and_14_out, C0, C1, C2, G0, G1, G2, G3, P0, P1, P2, P3;

  and and_1 (and_1_out, P0, in_5);
  xor xor_1 (P0, in_1, B0);
  xor xor_2 (P1, in_2, in_7);
  and and_2 (G0, in_1, B0);
  and and_3 (G1, in_2, in_7);
  or or_1 (C0, and_1_out, G0);
  and and_4 (and_4_out, in_5, P2, P0, P1);
  and and_5 (and_5_out, P1, P2, G0);
  and and_6 (and_6_out, P2, G1);
  or or_2 (C2, and_4_out, G2, and_6_out, and_5_out);
  xor xor_3 (P2, in_3, in_8);
  xor xor_4 (P3, in_4, in_9);
  and and_7 (G2, in_3, in_8);
  and and_8 (G3, in_4, in_9);
  and and_9 (and_9_out, P0, P1, in_5);
  and and_10 (and_10_out, P1, G0);
  and and_11 (and_11_out, in_5, P0, P1, P2, P3);
  and and_12 (and_12_out, P3, P2, P1, G0);
  and and_13 (and_13_out, P3, P2, G1);
  and and_14 (and_14_out, P3, G2);
  or or_3 (C1, and_9_out, G1, and_10_out);
  or or_4 (out_14, G3, and_11_out, and_12_out, and_13_out, and_14_out);
  full__adder full_adder_1 (.A(in_1), .B(B0), .Cin(in_5), .S(out_10));  // open: Co
  full__adder full_adder_2 (.A(in_4), .B(in_9), .Cin(C2), .S(out_13));  // open: Co
  full__adder full_adder_3 (.A(in_2), .B(in_7), .Cin(C0), .S(out_11));  // open: Co
  full__adder full_adder_4 (.A(in_3), .B(in_8), .Cin(C1), .S(out_12));  // open: Co

  // Other names for the same wires on the sheet: A0 = in_1; A1 = in_2; A2 = in_3; A3 = in_4; B1 = in_7; B2 = in_8;
  //   B3 = in_9; Cin = in_5; Cout = out_14; S0 = out_10; S1 = out_11; S2 = out_12; S3 = out_13

  // Notes on the sheet:
  //   C0
  //   C2
  //   generating variables
  //   C1
  //   Cout
  //   FOR BIT 0
  //   FOR BIT 3
  //   Predicting Carries
  //   Implementation
  //   FOR BIT 1
  //   FOR BIT 2
endmodule

module alu_main (
  input  SUB,
  input  EN,
  input  [7:0] in_3,
  input  [7:0] in_4,
  output [7:0] Result
);

  wire n4_b_1_out_10, n4_b_1_out_11, n4_b_1_out_12, n4_b_1_out_13, n4_b_1_out_14, n4_b_2_out_10,
       n4_b_2_out_11, n4_b_2_out_12, n4_b_2_out_13, xor_1_out, xor_2_out, xor_3_out, xor_4_out, xor_5_out,
       xor_6_out, xor_7_out, xor_8_out;

  xor xor_1 (xor_1_out, in_3[0], SUB);
  xor xor_2 (xor_2_out, in_3[1], SUB);
  xor xor_3 (xor_3_out, in_3[2], SUB);
  xor xor_4 (xor_4_out, in_3[3], SUB);
  xor xor_5 (xor_5_out, in_3[4], SUB);
  xor xor_6 (xor_6_out, in_3[5], SUB);
  xor xor_7 (xor_7_out, in_3[6], SUB);
  xor xor_8 (xor_8_out, in_3[7], SUB);
  _4_b u_4_b_1 (
    .in_1(in_4[0]), .in_2(in_4[1]), .in_3(in_4[2]), .in_4(in_4[3]), .B0(xor_1_out), .in_7(xor_2_out),
    .in_8(xor_3_out), .in_9(xor_4_out), .out_10(n4_b_1_out_10), .out_11(n4_b_1_out_11),
    .out_12(n4_b_1_out_12), .out_13(n4_b_1_out_13), .out_14(n4_b_1_out_14), .in_5(SUB));
  _4_b u_4_b_2 (
    .in_1(in_4[4]), .in_2(in_4[5]), .in_3(in_4[6]), .in_4(in_4[7]), .B0(xor_5_out), .in_7(xor_6_out),
    .in_8(xor_7_out), .in_9(xor_8_out), .out_10(n4_b_2_out_10), .out_11(n4_b_2_out_11),
    .out_12(n4_b_2_out_12), .out_13(n4_b_2_out_13), .in_5(n4_b_1_out_14));  // open: out_14
  assign Result[0] = EN ? n4_b_1_out_10 : 1'bz;  // Controlled_Buffer controlled_buffer_1
  assign Result[1] = EN ? n4_b_1_out_11 : 1'bz;  // Controlled_Buffer controlled_buffer_2
  assign Result[2] = EN ? n4_b_1_out_12 : 1'bz;  // Controlled_Buffer controlled_buffer_3
  assign Result[3] = EN ? n4_b_1_out_13 : 1'bz;  // Controlled_Buffer controlled_buffer_4
  assign Result[4] = EN ? n4_b_2_out_10 : 1'bz;  // Controlled_Buffer controlled_buffer_5
  assign Result[5] = EN ? n4_b_2_out_11 : 1'bz;  // Controlled_Buffer controlled_buffer_6
  assign Result[6] = EN ? n4_b_2_out_12 : 1'bz;  // Controlled_Buffer controlled_buffer_7
  assign Result[7] = EN ? n4_b_2_out_13 : 1'bz;  // Controlled_Buffer controlled_buffer_8

  // Other names for the same wires on the sheet: ENABLE = EN

  // Notes on the sheet:
  //   REGISTER B
  //   REGISTER A
  //   ALU
  //   RESULT
endmodule
